# Fritzing sketch zamok (saved by Fritzing 0.9.2b)
breadboards: 1

parts:
  S1 = Momentary Switch [package=ksa_sealed_tac_switch]
  S2 = Momentary Switch [package=ksa_sealed_tac_switch]
  S3 = Momentary Switch [package=ksa_sealed_tac_switch]
  Part1 = Arduino Nano (Rev3.0)

nets:
  N1: S1.1, Part1.D12/MISO
  N2: S1.3, S2.3, S3.3, Part1.D9
  N3: S2.1, Part1.D11/MOSI
  N4: S3.1, Part1.D10

// code stored in the sketch: zamok.ino
// hardware abstraction layer
#define 	COL1	12
#define 	COL2	11
#define 	COL3	10

#define 	ROW1	9

void setup() {
	pinMode(COL1, INPUT);
	pinMode(COL2, INPUT);
	pinMode(COL3, INPUT);

	pinMode(ROW1, OUTPUT);
}

void loop() {

}
