# Fritzing sketch sketch (saved by Fritzing 0.9.3b)
breadboards: 1

parts:
  WeMos_D1_Mini1 = WeMos D1 Mini
  Squix1 = OLED 0.96" 128x64 I2C SSD1306
  U1 = SUP500F [package=sup500f]

nets:
  VCC: WeMos_D1_Mini1.5V, Squix1.VCC, U1.VCC
  N1: WeMos_D1_Mini1.G, Squix1.GND

custom parts:
  WeMos D1 Mini: The D1 mini is a mini wifi board based on ESP-8266EX.
